# Fritzing sketch Diagrama de conexion (saved by Fritzing 0.9.3b)
breadboards: 1

parts:
  Componente1 = Arduino Uno (Rev3)
  FC-28 = FC-28 Soil Hygrometer Module
  BMP180 = Barometric Pressure Sensor - BMP180 Breakout (GY-68)
  R1 = Photocell (LDR) [package=THT]
  R2 = Resistor [tolerance=±5% resistance=10k package=THT]

nets:
  N1: Componente1.A0, FC-28.AO
  N2: Componente1.A1, R1.pin_1, R2.Pin_0
  N3: Componente1.A4/SDA, BMP180.SDA
  N4: Componente1.A5/SCL, BMP180.SCL
  VCC: Componente1.5V, FC-28.VCC, BMP180.VCC, R1.pin_0
  GND: Componente1.GND, FC-28.GND, BMP180.GND, R2.Pin_1

custom parts:
  FC-28 Soil Hygrometer Module: The FC-28 is a soil hygrometer module that uses the Texas Instruments LM393 comparator chip to provide an analog measurement of soil humidity. The digital output is high when soil moisture is over a certain threshold, as determined by adjusting the potentiometer.
